# Fritzing sketch ESP8266-Windsensor (saved by Fritzing 0.9.3b)
breadboards: 1

parts:
  U1 = NodeMCU V1.0
  S1 = Reed switch [package=THT]
  R1 = Resistor [tolerance=±5% resistance=330 package="0402 [SMD]"]
  OLED_I2C3 = OLED 128x64 I2C Monochrome Display

nets:
  N1: U1.D1, OLED_I2C3.SDA
  N2: U1.D2, OLED_I2C3.SCK
  N3: U1.D4, S1.pin_1, R1.Pin_0
  3V3: U1.3V3, S1.pin_2, OLED_I2C3.VDD
  GND: U1.GND, R1.Pin_1, OLED_I2C3.GND

custom parts:
  NodeMCU V1.0: ESP8266 based NodeMCU
